// Logisim project CPU.circ as structural Verilog: 14 circuits, main circuit CPU
module ALU (
  input  [15:0] A,
  input  [15:0] B,
  input  [3:0] sel,
  output [15:0] outputPin,
  output zr
);

  wire [0:0] comparator_2_eq;
  wire [15:0] adder_1_out, adder_2_out, adder_3_out, and_1_out, divider_1_out, multiplier_1_out,
       negator_1_out, not_1_out, or_1_out, shifter_1_out, shifter_2_out, shifter_3_out, shifter_4_out,
       subtractor_1_out, xor_1_out;

  assign and_1_out = A & B;  // AND_Gate and_1, 16 bits wide
  assign or_1_out = A | B;  // OR_Gate or_1, 16 bits wide
  assign not_1_out = ~A;  // NOT_Gate not_1, 16 bits wide
  assign xor_1_out = A ^ B;  // XOR_Gate xor_1, 16 bits wide
  Negator #(.width(16)) negator_1 (.in(A), .out(negator_1_out));
  Adder #(.width(16)) adder_1 (.a(A), .b(B), .out(adder_1_out));  // open: cin, cout
  Subtractor #(.width(16)) subtractor_1 (.a(A), .b(B), .out(subtractor_1_out));  // open: bin, bout
  Multiplier #(.width(16)) multiplier_1 (.a(A), .b(B), .out(multiplier_1_out));  // open: cin, cout
  Multiplexer #(.select(4), .width(16)) multiplexer_1 (
    .in0(and_1_out), .in1(or_1_out), .in2(xor_1_out), .in3(not_1_out), .in4(negator_1_out),
    .in5(adder_1_out), .in6(subtractor_1_out), .in7(multiplier_1_out), .in8(divider_1_out),
    .in9(adder_2_out), .in10(adder_3_out), .in11(shifter_1_out), .in12(shifter_2_out),
    .in13({{15{1'b0}}, comparator_2_eq[0]}), .in14(shifter_3_out), .in15(shifter_4_out), .out(outputPin),
    .sel(sel));
  Divider #(.width(16)) divider_1 (.a(A), .b(B), .out(divider_1_out));  // open: upper, rem
  Comparator #(.width(16)) comparator_1 (.a(outputPin), .b({16{1'b0}}), .eq(zr));  // open: gt, lt
  Adder #(.width(16)) adder_2 (.a(A), .b(16'h1), .out(adder_2_out));  // open: cin, cout
  Adder #(.width(16)) adder_3 (.a(A), .b(16'h1), .out(adder_3_out));  // open: cin, cout
  Shifter #(.width(16)) shifter_1 (.in(A), .\dist (4'b0001), .out(shifter_1_out));
  Shifter #(.shift("lr"), .width(16)) shifter_2 (.in(A), .\dist (4'b0001), .out(shifter_2_out));
  Comparator #(.width(16)) comparator_2 (.a(A), .b(B), .eq(comparator_2_eq[0]));  // open: gt, lt
  Shifter #(.shift("ar"), .width(16)) shifter_3 (.in(A), .\dist (B[3:0]), .out(shifter_3_out));
  Shifter #(.shift("rr"), .width(16)) shifter_4 (.in(A), .\dist (B[3:0]), .out(shifter_4_out));
endmodule

module DFlipFlop (
  input  D,
  input  clockPin,
  output Q,
  output NotQ
);

  wire nand_1_out, nand_2_out, not_1_out;

  not not_1 (not_1_out, D);
  nand nand_1 (nand_1_out, D, clockPin);
  nand nand_2 (nand_2_out, not_1_out, clockPin);
  nand nand_3 (Q, nand_1_out, NotQ);
  nand nand_4 (NotQ, Q, nand_2_out);
endmodule

module Bit (
  input  load,
  input  inputPin,
  input  clockPin,
  output outputPin
);

  wire multiplexer_1_out;

  Multiplexer multiplexer_1 (.in0(outputPin), .in1(inputPin), .out(multiplexer_1_out), .sel(load));
  DFlipFlop dflipflop_1 (.D(multiplexer_1_out), .clockPin(clockPin), .Q(outputPin));  // open: NotQ
endmodule

module BitRegister (
  input  [15:0] inputPin,
  input  load,
  input  clockPin,
  input  reset,
  output [15:0] outputPin
);

  wire [15:0] multiplexer_1_out;

  Multiplexer #(.width(16)) multiplexer_1 (.in0(outputPin), .in1(inputPin), .out(multiplexer_1_out), .sel(load));
  Register #(.width(16)) register_1 (.D(multiplexer_1_out), .clk(clockPin), .Q(outputPin), .clr(reset));  // open: en
endmodule

module RAM8 (
  input  clockPin,
  input  load,
  input  [2:0] address,
  input  [15:0] inputPin,
  output [15:0] outputPin
);

  wire demultiplexer_1_out0, demultiplexer_1_out1, demultiplexer_1_out2, demultiplexer_1_out3,
       demultiplexer_1_out4, demultiplexer_1_out5, demultiplexer_1_out6, demultiplexer_1_out7;
  wire [15:0] bitregister_1_p4, bitregister_2_p4, bitregister_3_p4, bitregister_4_p4, bitregister_5_p4,
       bitregister_6_p4, bitregister_7_p4, bitregister_8_p4;

  Demultiplexer #(.select(3), .tristate("true")) demultiplexer_1 (
    .out0(demultiplexer_1_out0), .out1(demultiplexer_1_out1), .out2(demultiplexer_1_out2),
    .out3(demultiplexer_1_out3), .out4(demultiplexer_1_out4), .out5(demultiplexer_1_out5),
    .out6(demultiplexer_1_out6), .out7(demultiplexer_1_out7), .in(load), .sel(address));
  // BitRegister bitregister_1: pin names not known; wires that end beside it: demultiplexer_1_out0, clockPin, inputPin, bitregister_1_p4
  // BitRegister bitregister_2: pin names not known; wires that end beside it: demultiplexer_1_out1, clockPin, inputPin, bitregister_2_p4
  // BitRegister bitregister_3: pin names not known; wires that end beside it: demultiplexer_1_out2, clockPin, inputPin, bitregister_3_p4
  // BitRegister bitregister_4: pin names not known; wires that end beside it: demultiplexer_1_out3, clockPin, inputPin, bitregister_4_p4
  // BitRegister bitregister_5: pin names not known; wires that end beside it: demultiplexer_1_out4, clockPin, inputPin, bitregister_5_p4
  // BitRegister bitregister_6: pin names not known; wires that end beside it: demultiplexer_1_out5, clockPin, inputPin, bitregister_6_p4
  // BitRegister bitregister_7: pin names not known; wires that end beside it: demultiplexer_1_out6, clockPin, inputPin, bitregister_7_p4
  // BitRegister bitregister_8: pin names not known; wires that end beside it: demultiplexer_1_out7, clockPin, inputPin, bitregister_8_p4
  Multiplexer #(.select(3), .width(16)) multiplexer_1 (
    .in0(bitregister_1_p4), .in1(bitregister_2_p4), .in2(bitregister_3_p4), .in3(bitregister_4_p4),
    .in4(bitregister_5_p4), .in5(bitregister_6_p4), .in6(bitregister_7_p4), .in7(bitregister_8_p4),
    .out(outputPin), .sel(address));
endmodule

module CPU (
  input  in_1,
  input  in_2,
  output [15:0] outputPin,
  output [15:0] out_4,
  output [15:0] out_5
);

  wire alu_1_zr, demultiplexer_1_out0, demultiplexer_1_out1, demultiplexer_1_out2, demultiplexer_1_out3,
       demultiplexer_1_out4, demultiplexer_1_out5, demultiplexer_1_out6, demultiplexer_1_out7,
       MasterClock_out, multiplexer_7_out, not_1_out, opcodechecker_1_arithmetic, opcodechecker_1_dbnxt,
       opcodechecker_1_je, opcodechecker_1_jmp, opcodechecker_1_ldr, opcodechecker_1_str, or_1_out, or_2_out,
       or_3_out;
  wire [2:0] InstructionMemory_p3_2, multiplexer_1_out, multiplexer_4_out;
  wire [3:0] InstructionMemory_p3_3;
  wire [14:0] adder_1_out, programcounter_1_outputpin;
  wire [15:0] alu_1_outputpin, DataMemory_dout, InstructionMemory_p3, InstructionMemory_p4,
       multiplexer_3_out, multiplexer_5_out, multiplexer_6_out, R0_outputpin, R2_outputpin, R3_outputpin,
       R4_outputpin, R5_outputpin, R6_outputpin, registermuxsimplification_1_outputpin,
       registermuxsimplification_2_outputpin;

  Adder #(.width(15)) adder_1 (.a(programcounter_1_outputpin), .b(15'h2), .out(adder_1_out));  // open: cin, cout
  not not_1 (not_1_out, or_3_out);
  ProgramCounter programcounter_1 (
    .inputPin(adder_1_out), .reset(in_2), .load(or_3_out), .increment(not_1_out), .clockPin(in_1),
    .outputPin(programcounter_1_outputpin));
  Clock MasterClock (.out(MasterClock_out));
  ALU alu_1 (
    .A(registermuxsimplification_2_outputpin), .B(registermuxsimplification_1_outputpin),
    .sel(InstructionMemory_p3_3), .outputPin(alu_1_outputpin), .zr(alu_1_zr));
  Demultiplexer #(.select(3)) demultiplexer_1 (
    .out0(demultiplexer_1_out0), .out1(demultiplexer_1_out1), .out2(demultiplexer_1_out2),
    .out3(demultiplexer_1_out3), .out4(demultiplexer_1_out4), .out5(demultiplexer_1_out5),
    .out6(demultiplexer_1_out6), .out7(demultiplexer_1_out7), .in(or_2_out), .sel(multiplexer_1_out));
  Multiplexer #(.width(3)) multiplexer_1 (
    .in0(InstructionMemory_p3_3[3:1]), .in1(InstructionMemory_p3_2), .out(multiplexer_1_out),
    .sel(opcodechecker_1_arithmetic));
  // ROM #(.addrWidth(15), .dataWidth(16), .line("dual")) InstructionMemory: pin names not known; wires that end beside it: MasterClock_out, programcounter_1_outputpin, {InstructionMemory_p3[15:11], InstructionMemory_p3_3, InstructionMemory_p3_2, InstructionMemory_p3[3:0]}, InstructionMemory_p4
  Multiplexer #(.width(16)) multiplexer_2 (
    .in0(multiplexer_3_out), .in1(alu_1_outputpin), .out(outputPin), .sel(opcodechecker_1_arithmetic));
  Multiplexer #(.width(16)) multiplexer_3 (
    .in0(multiplexer_5_out), .in1(InstructionMemory_p4), .out(multiplexer_3_out), .sel(opcodechecker_1_dbnxt));
  Multiplexer #(.width(3)) multiplexer_4 (
    .in0({InstructionMemory_p3_3[0], InstructionMemory_p3_2[2:1]}), .in1(InstructionMemory_p3[3:1]),
    .out(multiplexer_4_out), .sel(opcodechecker_1_arithmetic));
  OpCodeChecker opcodechecker_1 (
    .OpCode(InstructionMemory_p3[15:11]), .ldr(opcodechecker_1_ldr), .str(opcodechecker_1_str),
    .dbnxt(opcodechecker_1_dbnxt), .arithmetic(opcodechecker_1_arithmetic), .jmp(opcodechecker_1_jmp),
    .je(opcodechecker_1_je));  // open: swp, endcode, labelcode
  Multiplexer #(.width(16)) multiplexer_5 (
    .in0({16{1'b0}}), .in1(DataMemory_dout), .out(multiplexer_5_out), .sel(opcodechecker_1_ldr));
  Multiplexer #(.width(16)) multiplexer_6 (
    .in0({16{1'b0}}), .in1(registermuxsimplification_1_outputpin), .out(multiplexer_6_out), .sel(or_1_out));
  or or_1 (or_1_out, opcodechecker_1_ldr, opcodechecker_1_str);
  Multiplexer multiplexer_7 (.in0(1'b0), .in1(opcodechecker_1_je), .out(multiplexer_7_out), .sel(alu_1_zr));
  BitRegister R0 (
    .inputPin(outputPin), .load(demultiplexer_1_out0), .clockPin(in_1), .reset(in_2), .outputPin(R0_outputpin));
  BitRegister R1 (.inputPin(outputPin), .load(demultiplexer_1_out1), .clockPin(in_1), .reset(in_2), .outputPin(out_4));
  BitRegister R2 (
    .inputPin(outputPin), .load(demultiplexer_1_out2), .clockPin(in_1), .reset(in_2), .outputPin(R2_outputpin));
  BitRegister R3 (
    .inputPin(outputPin), .load(demultiplexer_1_out3), .clockPin(in_1), .reset(in_2), .outputPin(R3_outputpin));
  BitRegister R4 (
    .inputPin(outputPin), .load(demultiplexer_1_out4), .clockPin(in_1), .reset(in_2), .outputPin(R4_outputpin));
  BitRegister R5 (
    .inputPin(outputPin), .load(demultiplexer_1_out5), .clockPin(in_1), .reset(in_2), .outputPin(R5_outputpin));
  BitRegister R6 (
    .inputPin(outputPin), .load(demultiplexer_1_out6), .clockPin(in_1), .reset(in_2), .outputPin(R6_outputpin));
  BitRegister R7 (.inputPin(outputPin), .load(demultiplexer_1_out7), .clockPin(in_1), .reset(in_2), .outputPin(out_5));
  or or_2 (or_2_out, opcodechecker_1_ldr, opcodechecker_1_str, opcodechecker_1_dbnxt, opcodechecker_1_arithmetic);
  or or_3 (or_3_out, opcodechecker_1_dbnxt, opcodechecker_1_jmp, multiplexer_7_out);
  RegisterMUXSimplification registermuxsimplification_1 (
    .R0toR3({R0_outputpin, out_4, R2_outputpin, R3_outputpin}),
    .R4toR7({R4_outputpin, R5_outputpin, R6_outputpin, out_5}), .sel(multiplexer_4_out),
    .outputPin(registermuxsimplification_1_outputpin));
  RegisterMUXSimplification registermuxsimplification_2 (
    .R0toR3({R0_outputpin, out_4, R2_outputpin, R3_outputpin}),
    .R4toR7({R4_outputpin, R5_outputpin, R6_outputpin, out_5}), .sel(multiplexer_1_out),
    .outputPin(registermuxsimplification_2_outputpin));
  RAM #(.addrWidth(16), .dataWidth(16)) DataMemory (
    .addr(multiplexer_6_out), .we(opcodechecker_1_str), .oe(opcodechecker_1_ldr), .clk(in_1),
    .din(registermuxsimplification_2_outputpin), .dout(DataMemory_dout));

  // Notes on the sheet:
  //   contents of InstructionMemory (hex, n*v repeats v):
  //   3700 3700
endmodule

module PixelCounter (
  input  clockPin,
  input  reset,
  output [15:0] address,
  output [6:0] XOutput,
  output [6:0] YOutput
);

  wire XCounter_carry;
  wire [8:0] XCounter_q, YCounter_q;

  Counter #(.max('h7f), .width(16)) XCounter (
    .Q({XCounter_q, XOutput}), .carry(XCounter_carry), .clk(clockPin), .clr(reset));  // open: load, D, count, up
  Counter #(.max('h7f), .trigger("falling"), .width(16)) YCounter (
    .Q({YCounter_q, YOutput}), .clk(XCounter_carry), .clr(reset));  // open: load, D, count, carry, up
  Multiplier #(.width(16)) multiplier_1 (
    .a({YCounter_q, YOutput}), .b(16'h14), .out(address), .cin({XCounter_q, XOutput}));  // open: cout
endmodule

module Screen (
  input  in_1,
  input  [15:0] in_2,
  input  clockPin,
  input  reset,
  input  writeEnable
);

  wire [6:0] pixelcounter_1_xoutput, pixelcounter_1_youtput;
  wire [15:0] pixelcounter_1_address, ScreenMemory_dout;

  PixelCounter pixelcounter_1 (
    .clockPin(clockPin), .reset(reset), .address(pixelcounter_1_address), .XOutput(pixelcounter_1_xoutput),
    .YOutput(pixelcounter_1_youtput));
  RAM #(.addrWidth(16), .dataWidth(16)) ScreenMemory (
    .addr(pixelcounter_1_address), .we(in_1), .oe(in_1), .clk(clockPin), .din(in_2), .dout(ScreenMemory_dout));
  // RGB_Video #(.cursor("No Cursor"), .scale(8)) rgb_video_1: pin names not known; wires that end beside it: clockPin, writeEnable, pixelcounter_1_xoutput, pixelcounter_1_youtput, ScreenMemory_dout
endmodule

module ProgramCounter (
  input  [14:0] inputPin,
  input  reset,
  input  load,
  input  increment,
  input  clockPin,
  output [14:0] outputPin
);

  wire or_1_out, or_2_out;
  wire [14:0] adder_1_out, multiplexer_1_out, multiplexer_2_out, multiplexer_3_out, multiplexer_4_out;

  Adder #(.width(15)) adder_1 (.a(outputPin), .b(15'h1), .out(adder_1_out));  // open: cin, cout
  Multiplexer #(.width(15)) multiplexer_1 (
    .in0(outputPin), .in1(adder_1_out), .out(multiplexer_1_out), .sel(increment));
  Multiplexer #(.width(15)) multiplexer_2 (
    .in0(multiplexer_1_out), .in1(inputPin), .out(multiplexer_2_out), .sel(load));
  Multiplexer #(.width(15)) multiplexer_3 (
    .in0(multiplexer_2_out), .in1({15{1'b0}}), .out(multiplexer_3_out), .sel(reset));
  or or_1 (or_1_out, load, increment);
  or or_2 (or_2_out, or_1_out, reset);
  Multiplexer #(.width(15)) multiplexer_4 (
    .in0(outputPin), .in1(multiplexer_3_out), .out(multiplexer_4_out), .sel(or_2_out));
  Register #(.width(15)) register_1 (.D(multiplexer_4_out), .clk(clockPin), .Q(outputPin));  // open: en, clr
endmodule

module InstructionDecoder (
  input  [10:0] flags,
  input  [4:0] OpCode,
  output [2:0] out_3,
  output [15:0] AddressBus
);

  OpCodeChecker opcodechecker_1 (.OpCode(OpCode));  // open: ldr, str, dbnxt, swp, arithmetic, jmp, je, endcode, labelcode
  Multiplexer #(.width(16)) multiplexer_1 (.in1({16{1'b0}}), .out(AddressBus));  // open: in0, sel

  assign out_3 = flags[10:8];
endmodule

module OpCodeChecker (
  input  [4:0] OpCode,
  output ldr,
  output str,
  output dbnxt,
  output swp,
  output arithmetic,
  output jmp,
  output je,
  output endcode,
  output labelcode
);

  wire not_1_out, not_2_out, not_3_out, not_4_out, not_5_out;

  not not_1 (not_1_out, OpCode[4]);
  not not_2 (not_2_out, OpCode[3]);
  not not_3 (not_3_out, OpCode[2]);
  not not_4 (not_4_out, OpCode[1]);
  not not_5 (not_5_out, OpCode[0]);
  and and_1 (ldr, not_1_out, not_2_out, not_3_out, not_4_out, not_5_out);
  and and_2 (str, not_1_out, not_2_out, not_3_out, not_4_out, OpCode[0]);
  and and_3 (dbnxt, not_1_out, not_2_out, not_3_out, OpCode[1], not_5_out);
  and and_4 (swp, not_1_out, not_2_out, not_3_out, OpCode[1], OpCode[0]);
  and and_5 (arithmetic, not_1_out, not_2_out, OpCode[2], not_4_out, not_5_out);
  and and_6 (jmp, not_1_out, not_2_out, OpCode[2], not_4_out, OpCode[0]);
  and and_7 (je, not_1_out, not_2_out, OpCode[2], OpCode[1], not_5_out);
  and and_8 (endcode, not_1_out, not_2_out, OpCode[2], OpCode[1], OpCode[0]);
  and and_9 (labelcode, not_1_out, OpCode[3], not_3_out, not_4_out, not_5_out);
endmodule

module RegisterMUXSimplification (
  input  [63:0] R0toR3,
  input  [63:0] R4toR7,
  input  [2:0] sel,
  output [15:0] outputPin
);

  Multiplexer #(.select(3), .width(16)) multiplexer_1 (
    .in0(R0toR3[63:48]), .in1(R0toR3[47:32]), .in2(R0toR3[31:16]), .in3(R0toR3[15:0]), .in4(R4toR7[63:48]),
    .in5(R4toR7[47:32]), .in6(R4toR7[31:16]), .in7(R4toR7[15:0]), .out(outputPin), .sel(sel));
endmodule

module ArithmeticInstructionToALU (
  input  [8:0] operations,
  output zx,
  output nx,
  output zy,
  output ny,
  output f,
  output no
);

  or or_1 (no, operations[8], operations[7], operations[5], operations[2], operations[1]);
  or or_2 (f, operations[8], operations[3], operations[2], operations[1], operations[0]);
  or or_3 (ny, operations[8], operations[7], operations[5], operations[3], operations[2]);
  or or_4 (zy, operations[8], operations[7], operations[3], operations[2]);
  or or_5 (nx, operations[8], operations[5], operations[3], operations[2], operations[1]);

  assign zx = 1'b0;
endmodule

module OldALU (
  input  zx,
  input  nx,
  input  zy,
  input  ny,
  input  f,
  input  no,
  input  [15:0] in_7,
  input  [15:0] in_8,
  output zr,
  output ng,
  output [15:0] out_11
);

  wire or_1_out;
  wire [15:0] adder_1_out, and_1_out, multiplexer_1_out, multiplexer_2_out, multiplexer_3_out,
       multiplexer_4_out, multiplexer_5_out, not_1_out, not_2_out, not_3_out;

  Multiplexer #(.width(16)) multiplexer_1 (.in0(in_7), .in1({16{1'b0}}), .out(multiplexer_1_out), .sel(zx));
  Multiplexer #(.width(16)) multiplexer_2 (.in0(in_8), .in1({16{1'b0}}), .out(multiplexer_2_out), .sel(zy));
  assign not_1_out = ~multiplexer_1_out;  // NOT_Gate not_1, 16 bits wide
  assign not_2_out = ~multiplexer_2_out;  // NOT_Gate not_2, 16 bits wide
  Multiplexer #(.width(16)) multiplexer_3 (.in0(multiplexer_1_out), .in1(not_1_out), .out(multiplexer_3_out), .sel(nx));
  Multiplexer #(.width(16)) multiplexer_4 (.in0(multiplexer_2_out), .in1(not_2_out), .out(multiplexer_4_out), .sel(ny));
  assign and_1_out = multiplexer_3_out & multiplexer_4_out;  // AND_Gate and_1, 16 bits wide
  Adder #(.width(16)) adder_1 (.a(multiplexer_3_out), .b(multiplexer_4_out), .out(adder_1_out));  // open: cin, cout
  Multiplexer #(.width(16)) multiplexer_5 (.in0(and_1_out), .in1(adder_1_out), .out(multiplexer_5_out), .sel(f));
  assign not_3_out = ~multiplexer_5_out;  // NOT_Gate not_3, 16 bits wide
  Multiplexer #(.width(16)) multiplexer_6 (
    .in0(multiplexer_5_out), .in1(not_3_out), .out({ng, out_11[14:0]}), .sel(no));
  or or_1 (or_1_out, out_11[0], out_11[1], out_11[2], out_11[3], out_11[4], out_11[5], out_11[6], out_11[7], out_11[8], out_11[9], out_11[10], out_11[11], out_11[12], out_11[13], out_11[14], ng);
  not not_4 (zr, or_1_out);

  assign out_11[15] = ng;
endmodule
